// Logisim project parts.circ as structural Verilog: 10 circuits, main circuit main
module main (
  input  seq_clr,
  input  ir_we,
  input  in_3,
  input  imem_reset,
  input  main_clk,
  input  f_reset,
  input  acc_clr,
  input  dmem_clr,
  output [7:0] out_9,
  output [7:0] out_10,
  output [7:0] out_11,
  output [7:0] out_12,
  output [7:0] out_13
);

  wire not_1_out, or_1_out, or_2_out, or_3_out, or_4_out, or_5_out;
  wire [1:0] bit_extender_1_out;
  wire [2:0] n3msb_ir_1__3_msb_out;
  wire [3:0] adder_1_out, multiplexer_1_out, seq_1_fetch, seq_1_inst;
  wire [4:0] bit_extender_2_out;
  wire [7:0] alu_1_out_6, controlled_buffer_2_out, controlled_buffer_3_out, ram_2_data, ram_4_data,
       reg_d_right_1_q;
  wire [11:0] ram_1_data;

  or or_1 (or_1_out, ram_1_data[10], f_reset);
  program_counter program_counter_1 (
    .pc_we(ram_1_data[8]), .clk(main_clk), .pc_re(ram_4_data[0]), .pc_in(out_13), .pc_clr(or_1_out),
    .inc(ram_1_data[11]), .pc_out(out_11));
  or or_2 (or_2_out, ram_1_data[7], f_reset);
  register register_1 (
    .we(ram_1_data[5]), .re(ram_1_data[6]), .d_in(out_11), .clk(main_clk), .clr(or_2_out), .d_out(out_12));
  RAM #(.addrWidth(2), .dataWidth(12)) ram_1 (
    .addr(bit_extender_1_out), .data(ram_1_data), .clk(main_clk));  // open: sel, ld, clr
  RAM ram_2 (.addr(out_12), .data(ram_2_data), .clk(main_clk), .clr(or_3_out));  // open: sel, ld
  or or_3 (or_3_out, ram_1_data[4], imem_reset);
  seq seq_1 (.clk(main_clk), .fetch(seq_1_fetch), .inst(seq_1_inst), .seq_clr(seq_clr));
  assign out_10 = ram_1_data[3] ? ram_2_data : 8'bz;  // Controlled_Buffer controlled_buffer_1
  Bit_Extender #(.in_width(4), .out_width(2)) bit_extender_1 (.in(seq_1_fetch), .out(bit_extender_1_out));
  or or_4 (or_4_out, ram_1_data[2], f_reset);
  register register_2 (.we(ir_we), .re(ram_1_data[1]), .d_in(out_10), .clk(main_clk), .clr(or_4_out), .d_out(out_9));
  Multiplexer #(.select(3), .width(4), .enable("false")) multiplexer_1 (
    .in0(4'b0000), .in1(4'b1000), .in2(4'b0000), .in3(4'b0000), .in4(4'b0100), .in5(4'b0000), .in6(4'b0000),
    .in7(4'b0000), .out(multiplexer_1_out), .sel(n3msb_ir_1__3_msb_out));
  _3msb_ir u_3msb_ir_1 (._8_in(out_9), ._3_msb_out(n3msb_ir_1__3_msb_out));
  Bit_Extender #(.out_width(5)) bit_extender_2 (.in(out_9), .out(bit_extender_2_out));
  not not_1 (not_1_out, ram_4_data[6]);
  Adder #(.width(4)) adder_1 (.a(multiplexer_1_out), .b(seq_1_inst), .out(adder_1_out));  // open: cin, cout
  assign controlled_buffer_2_out = ram_4_data[4] ? reg_d_right_1_q : 8'bz;  // Controlled_Buffer controlled_buffer_2
  assign controlled_buffer_3_out = ram_4_data[5] ? controlled_buffer_2_out : 8'bz;  // Controlled_Buffer controlled_buffer_3
  RAM #(.addrWidth(5)) ram_3 (
    .addr(bit_extender_2_out), .data(controlled_buffer_2_out), .clk(main_clk), .ld(not_1_out), .clr(dmem_clr));  // open: sel
  RAM #(.addrWidth(4)) ram_4 (.addr(adder_1_out), .data(ram_4_data), .clk(main_clk));  // open: sel, ld, clr
  reg_d_right reg_d_right_1 (.en(ram_4_data[4]), .q(reg_d_right_1_q), .clk(main_clk), .d(out_13));
  alu alu_1 (
    .ir_sel(out_9), .clk(main_clk), .alu_en(ram_4_data[3]), .out_6(alu_1_out_6),
    .dmem(controlled_buffer_3_out), .acc(out_13));
  or or_5 (or_5_out, ram_4_data[1], in_3);
  register register_3 (
    .we(or_5_out), .re(ram_4_data[2]), .d_in(alu_1_out_6), .clk(main_clk), .clr(acc_clr), .d_out(out_13));

  // Notes on the sheet:
  //   pc_inc
  //   pc_clr
  //   pc_we
  //   imr_clr
  //   imr_re
  //   imr_we
  //   imem_clr
  //   imr
  //   imem_we
  //   ir_clr
  //   ir_re
  //   ir_we
  //   ir
  //   dmem_re
  //   d_al
  //   LE
  //   alu_en
  //   acc_re
  //   acc_we
  //   acc
  //   pc_re
endmodule

module program_counter (
  input  pc_we,
  input  clk,
  input  pc_re,
  input  [7:0] pc_in,
  input  pc_clr,
  input  inc,
  output [7:0] pc_out
);

  wire not_1_out;
  wire [7:0] adder_1_out, controlled_buffer_1_out, multiplexer_1_out, register_1_q;

  Pull_Resistor pull_resistor_1 (.node(pc_re));
  assign controlled_buffer_1_out = pc_re ? pc_in : 8'bz;  // Controlled_Buffer controlled_buffer_1
  Register register_1 (.D(controlled_buffer_1_out), .Q(register_1_q), .clk(clk), .clr(pc_clr));  // open: en
  Multiplexer #(.width(8)) multiplexer_1 (.in0({8{1'b0}}), .in1(8'h1), .out(multiplexer_1_out), .sel(inc));  // open: en
  assign pc_out = pc_we ? register_1_q : 8'bz;  // Controlled_Buffer controlled_buffer_2
  Adder adder_1 (.a(register_1_q), .b(multiplexer_1_out), .out(adder_1_out));  // open: cin, cout
  assign controlled_buffer_1_out = not_1_out ? adder_1_out : 8'bz;  // Controlled_Buffer controlled_buffer_3
  not not_1 (not_1_out, pc_re);
endmodule

module register (
  input  we,
  input  re,
  input  [7:0] d_in,
  input  clk,
  input  clr,
  output [7:0] d_out
);

  wire [7:0] controlled_buffer_1_out, register_1_q;

  assign controlled_buffer_1_out = re ? d_in : 8'bz;  // Controlled_Buffer controlled_buffer_1
  Register register_1 (.D(controlled_buffer_1_out), .Q(register_1_q), .clk(clk), .clr(clr));  // open: en
  assign d_out = we ? register_1_q : 8'bz;  // Controlled_Buffer controlled_buffer_2
endmodule

module fetch_datapath (
  input  in_1,
  input  ir_we,
  input  imem_reset,
  input  main_clk,
  input  reset,
  output [7:0] ir,
  output [7:0] out_7,
  output [7:0] out_8,
  output [7:0] out_9
);

  wire or_1_out, or_2_out, or_3_out, or_4_out;
  wire [1:0] counter_1_q;
  wire [7:0] ram_2_data;
  wire [11:0] ram_1_data;

  Counter #(.width(2), .max('h3)) counter_1 (
    .Q(counter_1_q), .clk(main_clk), .clr(in_1));  // open: load, D, count, carry
  or or_1 (or_1_out, ram_1_data[10], reset);
  program_counter program_counter_1 (
    .pc_we(ram_1_data[8]), .clk(main_clk), .pc_clr(or_1_out), .inc(ram_1_data[11]), .pc_out(out_8));  // open: pc_re, pc_in
  or or_2 (or_2_out, ram_1_data[7], reset);
  register register_1 (
    .we(ram_1_data[5]), .re(ram_1_data[6]), .d_in(out_8), .clk(main_clk), .clr(or_2_out), .d_out(out_9));
  RAM #(.addrWidth(2), .dataWidth(12)) ram_1 (
    .addr(counter_1_q), .data(ram_1_data), .clk(main_clk));  // open: sel, ld, clr
  RAM ram_2 (.addr(out_9), .data(ram_2_data), .clk(main_clk), .clr(or_3_out));  // open: sel, ld
  or or_3 (or_3_out, ram_1_data[4], imem_reset);
  assign out_7 = ram_1_data[3] ? ram_2_data : 8'bz;  // Controlled_Buffer controlled_buffer_1
  or or_4 (or_4_out, ram_1_data[2], reset);
  register register_2 (.we(ir_we), .re(ram_1_data[1]), .d_in(out_7), .clk(main_clk), .clr(or_4_out), .d_out(ir));

  // Notes on the sheet:
  //   pc_inc
  //   pc_clr
  //   pc_we
  //   imr_clr
  //   imr_re
  //   imr_we
  //   fetch control memory
  //   imem_clr
  //   imr
  //   imem_we
  //   ir_clr
  //   ir_re
  //   ir_we
endmodule

module inst_datapath (
  input  in_1,
  input  ir_we,
  input  ir_re,
  input  pc_we,
  input  [7:0] in_5,
  input  in_6,
  input  clk,
  input  acc_clr,
  input  pc_clr,
  input  dmem_clr,
  output [7:0] pc,
  output [7:0] out_12
);

  wire not_1_out;
  wire [1:0] counter_1_q;
  wire [2:0] n3msb_ir_1__3_msb_out;
  wire [3:0] adder_1_out, bit_extender_2_out, multiplexer_1_out;
  wire [4:0] bit_extender_1_out;
  wire [7:0] alu_1_out_6, controlled_buffer_2_out, ram_1_data, ram_2_data, reg_d_right_1_q, register_1_d_out;

  _3msb_ir u_3msb_ir_1 (._8_in(register_1_d_out), ._3_msb_out(n3msb_ir_1__3_msb_out));
  register register_1 (.we(ir_we), .re(ir_re), .d_in(in_5), .clk(in_6), .d_out(register_1_d_out));  // open: clr
  Multiplexer #(.select(3), .width(4), .enable("false")) multiplexer_1 (
    .in0(4'b0000), .in1(4'b1000), .in2(4'b0000), .in3(4'b0000), .in4(4'b0100), .in5(4'b0000), .in6(4'b0000),
    .in7(4'b0000), .out(multiplexer_1_out), .sel(n3msb_ir_1__3_msb_out));
  Counter #(.width(2), .max('h3)) counter_1 (.Q(counter_1_q), .clk(clk), .clr(in_1));  // open: load, D, count, carry
  Bit_Extender #(.out_width(5)) bit_extender_1 (.in(register_1_d_out), .out(bit_extender_1_out));
  assign bit_extender_2_out = {{2{1'b0}}, counter_1_q};  // Bit_Extender bit_extender_2
  not not_1 (not_1_out, ram_2_data[6]);
  Adder #(.width(4)) adder_1 (.a(multiplexer_1_out), .b(bit_extender_2_out), .out(adder_1_out));  // open: cin, cout
  RAM #(.addrWidth(5)) ram_1 (
    .addr(bit_extender_1_out), .data(ram_1_data), .clk(clk), .ld(not_1_out), .clr(dmem_clr));  // open: sel
  reg_d_right reg_d_right_1 (.en(ram_2_data[4]), .q(reg_d_right_1_q), .clk(clk), .d(out_12));
  assign ram_1_data = ram_2_data[4] ? reg_d_right_1_q : 8'bz;  // Controlled_Buffer controlled_buffer_1
  assign controlled_buffer_2_out = ram_2_data[5] ? ram_1_data : 8'bz;  // Controlled_Buffer controlled_buffer_2
  RAM #(.addrWidth(4)) ram_2 (.addr(adder_1_out), .data(ram_2_data), .clk(clk));  // open: sel, ld, clr
  alu alu_1 (
    .ir_sel(register_1_d_out), .clk(clk), .alu_en(ram_2_data[3]), .out_6(alu_1_out_6),
    .dmem(controlled_buffer_2_out), .acc(out_12));
  register register_2 (
    .we(ram_2_data[1]), .re(ram_2_data[2]), .d_in(alu_1_out_6), .clk(clk), .clr(acc_clr), .d_out(out_12));
  register register_3 (.we(pc_we), .re(ram_2_data[0]), .d_in(out_12), .clk(clk), .clr(pc_clr), .d_out(pc));

  // Notes on the sheet:
  //   ir
  //   dmem_re
  //   d_al
  //   LE
  //   instruction control memory
  //   alu_en
  //   acc_we
  //   acc_re
  //   acc
  //   pc_re
endmodule

module alu (
  input  [7:0] dmem,
  input  alu_en,
  input  [7:0] acc,
  input  [7:0] ir_sel,
  input  clk,
  output [7:0] out_6
);

  wire [7:0] adder_1_out, adder_2_out, and_1_out, multiplexer_1_out, not_1_out, or_1_out, register_1_q,
       subtractor_1_out;

  Register register_1 (.D(dmem), .Q(register_1_q), .clk(clk));  // open: en, clr
  assign not_1_out = ~acc;  // NOT_Gate not_1, 8 bits wide
  Adder adder_1 (.a(register_1_q), .b(acc), .out(adder_1_out));  // open: cin, cout
  Subtractor subtractor_1 (.a(register_1_q), .b(acc), .out(subtractor_1_out));  // open: bin, bout
  Adder adder_2 (.a(8'h1), .b(acc), .out(adder_2_out));  // open: cin, cout
  assign and_1_out = register_1_q & acc;  // AND_Gate and_1, 8 bits wide
  assign or_1_out = register_1_q | acc;  // OR_Gate or_1, 8 bits wide
  Multiplexer #(.select(3), .width(8), .enable("false")) multiplexer_1 (
    .in0(adder_1_out), .in1({8{1'b0}}), .in2(subtractor_1_out), .in3(adder_2_out), .in4({8{1'b0}}),
    .in5(and_1_out), .in6(or_1_out), .in7(not_1_out), .out(multiplexer_1_out), .sel(ir_sel[7:5]));
  register register_2 (.we(alu_en), .re(1'b1), .d_in(multiplexer_1_out), .clk(clk), .d_out(out_6));  // open: clr
endmodule

module dir_bus (
  input  [7:0] in_1,
  input  in_2,
  output [7:0] out_3
);

  wire not_1_out;

  assign in_1 = not_1_out ? out_3 : 8'bz;  // Controlled_Buffer controlled_buffer_1
  assign out_3 = in_2 ? in_1 : 8'bz;  // Controlled_Buffer controlled_buffer_2
  not not_1 (not_1_out, in_2);
endmodule

module reg_d_right (
  input  [7:0] d,
  input  en,
  input  clk,
  output [7:0] q
);

  Register register_1 (.D(d), .en(en), .Q(q), .clk(clk));  // open: clr
endmodule

module _3msb_ir (
  input  [7:0] _8_in,
  output [2:0] _3_msb_out
);


  assign _3_msb_out = _8_in[7:5];
endmodule

module seq (
  input  clk,
  input  seq_clr,
  output [3:0] fetch,
  output [3:0] inst
);

  wire and_1_out, and_2_out, and_3_out, not_1_out, not_2_out, not_3_out, not_4_out, not_5_out, not_6_out,
       or_1_out;
  wire [3:0] controlled_buffer_1_out, counter_1_q;

  Counter #(.width(4), .max('hf)) counter_1 (
    .Q(counter_1_q), .clk(clk), .clr(or_1_out));  // open: load, D, count, carry
  or or_1 (or_1_out, and_3_out, seq_clr);
  not not_1 (not_1_out, counter_1_q[3]);
  and and_1 (and_1_out, not_1_out, not_3_out);
  not not_2 (not_2_out, counter_1_q[3]);
  and and_2 (and_2_out, not_2_out, counter_1_q[2]);
  not not_3 (not_3_out, counter_1_q[2]);
  assign controlled_buffer_1_out = and_2_out ? counter_1_q : 4'bz;  // Controlled_Buffer controlled_buffer_1
  assign fetch = and_1_out ? counter_1_q : 4'bz;  // Controlled_Buffer controlled_buffer_2
  not not_4 (not_4_out, counter_1_q[0]);
  not not_5 (not_5_out, counter_1_q[2]);
  not not_6 (not_6_out, counter_1_q[1]);
  and and_3 (and_3_out, counter_1_q[3], not_5_out, not_6_out, not_4_out);
  Subtractor #(.width(4)) subtractor_1 (.a(controlled_buffer_1_out), .b(4'b0100), .out(inst));  // open: bin, bout
endmodule
